# Fritzing sketch Our Project Sketch (saved by Fritzing 0.9.3b)
breadboards: 1

parts:
  LCD1 = Adafruit Negative RGB 2x16 LCD
  Part1 = Arduino Uno (Rev3)
  Mod1 = sensor_biometrico
  R1 = Resistor [tolerance=±5% resistance=220 package=THT]
  R2 = Resistor [tolerance=±5% resistance=220 package=THT]
  Keypad4x1 = Keypad Membran 4x4
  R3 = Resistor [tolerance=±5% resistance=220 package=THT]
  R4 = Resistor [tolerance=±5% resistance=220 package=THT]
  LED1 = LED - 5mm [color="Red (633nm)" package="5 mm [THT]"]
  LED2 = LED - 5mm [color="Green (565nm)" package="5 mm [THT]"]

nets:
  GND: LCD1.no_name_yet#100, LCD1.no_name_yet#104, Part1.GND, Mod1.GND, R1.Pin_0, R2.Pin_0, LED1.cathode, LED2.anode
  N1: LCD1.no_name_yet#101, LCD1.no_name_yet#114, Part1.5V
  N2: LCD1.no_name_yet#102, R2.Pin_1
  N3: LCD1.no_name_yet#103, Part1.A4/SDA
  N4: LCD1.no_name_yet#105, Part1.A5/SCL
  N5: LCD1.no_name_yet#110, Part1.D7
  N6: LCD1.no_name_yet#111, Part1.D6_PWM
  N7: LCD1.no_name_yet#112, Part1.D5_PWM
  N8: LCD1.no_name_yet#113, Part1.D4
  N9: LCD1.no_name_yet#115, R1.Pin_1
  N10: Part1.A0, Keypad4x1.Pin1
  N11: Part1.A1, Keypad4x1.Pin2
  N12: Part1.A2, Keypad4x1.Pin3
  N13: Part1.A3, Keypad4x1.Pin4
  N14: Part1.D8, Keypad4x1.Pin5
  N15: Part1.D9_PWM, Keypad4x1.Pin6
  N16: Part1.D10_PWM/SS, Keypad4x1.Pin7
  N17: Part1.D11_PWM/MOSI, Keypad4x1.Pin8
  N18: Part1.D2, Mod1.VCC
  N19: Part1.D3_PWM, Mod1.TX
  N20: Part1.3V3, Mod1.RX
  N21: R3.Pin_0, LED1.anode
  N22: R4.Pin_1, LED2.cathode

custom parts:
  Adafruit Negative RGB 2x16 LCD: Adafruit Negative 2x16 LCD Display with RGB Backlight
  sensor_biometrico: Adafruit Optical Fingerprint Sensor
  Keypad Membran 4x4: Membrane Keypad 4x4 Matrix
